// Logisim project logisim.circ as structural Verilog: 5 circuits, main circuit Problem 2
module Problem_2 (
);

  wire A_C_2_out, A_C_out, and_1_out, and_2_out, AND_3__3, AND_3__6, AND_3__8, AND_3__11, and_4_out,
       and_5_out, Initialize_2_out, Initialize_out, nor_2_out, nor_3_out, NOR_4__1, NOR_4__4, NOR_4__10,
       NOR_4__13, nor_5_out, nor_6_out, NOR_7__1, NOR__1, NOR__4, NOR__10, NOR__13, not_1_out, not_2_out,
       not_3_out, or_1_out;

  Button Initialize (.out(Initialize_out));
  Button A_C (.out(A_C_out));
  Button Initialize_2 (.out(Initialize_2_out));
  Button A_C_2 (.out(A_C_2_out));
  not not_1 (not_1_out, A_C_out);
  _7402 NOR (
    ._2(A_C_2_out), ._3(1'b0), ._5(NOR_4__13), ._6(1'b0), ._8(NOR_4__4), ._9(1'b0), ._11(NOR_7__1),
    ._12(1'b0), ._1(NOR__1), ._4(NOR__4), ._10(NOR__10), ._13(NOR__13));
  and and_1 (and_1_out, nor_6_out, not_1_out);
  not not_2 (not_2_out, nor_6_out);
  and and_2 (and_2_out, not_2_out, not_1_out);
  _7408 AND_3 (
    ._1(NOR__4), ._2(NOR__1), ._4(NOR_4__13), ._5(NOR__1), ._9(NOR__10), ._10(A_C_2_out), ._12(NOR_4__4),
    ._13(A_C_2_out), ._3(AND_3__3), ._6(AND_3__6), ._8(AND_3__8), ._11(AND_3__11));
  nor nor_2 (nor_2_out, and_1_out, nor_3_out);
  nor nor_3 (nor_3_out, nor_2_out, and_2_out);
  not not_3 (not_3_out, nor_3_out);
  and and_4 (and_4_out, nor_3_out, A_C_out);
  _7402 NOR_4 (
    ._2(AND_3__6), ._3(NOR_4__4), ._5(NOR_4__1), ._6(AND_3__3), ._8(AND_3__8), ._9(NOR_4__13),
    ._11(AND_3__11), ._12(NOR__13), ._1(NOR_4__1), ._4(NOR_4__4), ._10(NOR_4__10), ._13(NOR_4__13));
  and and_5 (and_5_out, not_3_out, A_C_out);
  nor nor_5 (nor_5_out, and_5_out, nor_6_out);
  or or_1 (or_1_out, Initialize_out, nor_5_out);
  nor nor_6 (nor_6_out, or_1_out, and_4_out);
  _7402 NOR_7 (._2(NOR_4__10), ._3(Initialize_2_out), ._1(NOR_7__1));  // open: _5, _6, _8, _9, _11, _12, _4, _10, _13
  LED A_C_On (.in(nor_6_out));
  LED A_C_On_2 (.in(NOR_4__13));

  // Notes on the sheet:
  //   Only push this button if red lines are visible
  //   7408 for AND gates, all pins used
  //   7402 for NOR gates, all pins used
  //   7402 is also needed for initializing the circuit, pins 1,2,3 used 
  //   7402 for NOT/OR gate simulation: pins 1,2,4,5 used for single input NOR gates (i.e. NOT gates) and 8,9,11,13 used to emulate a OR gate by chaining two NORs together
endmodule

module Problem_3 (
  input  Reset,
  input  I_O_Enable,
  input  _1_Bit,
  input  _2_Bit,
  input  _4_Bit,
  input  _8_Bit,
  output A_C,
  output D0,
  output D1,
  output D2,
  output D3,
  output Engine_Starter,
  output Wipers
);

  IO_Controller IO_Controller (
    .Reset(Reset), .IO_Enable(I_O_Enable), ._1_bit(_1_Bit), ._2_bit(_2_Bit), ._4_bit(_4_Bit),
    ._8_bit(_8_Bit), .A_C(A_C), .D0(D0), .D1(D1), .D2(D2), .D3(D3), .Engine_Starter(Engine_Starter),
    .Wipers(Wipers));

  // Notes on the sheet:
  //   Micro Controller
endmodule

module IO_Controller (
  input  Reset,
  input  IO_Enable,
  input  _1_bit,
  input  _2_bit,
  input  _4_bit,
  input  _8_bit,
  output A_C,
  output D0,
  output D1,
  output D2,
  output D3,
  output Engine_Starter,
  output Wipers
);

  wire and_1_out, and_2_out, and_3_out, and_4_out, and_5_out, and_6_out, and_7_out, and_8_out, and_9_out,
       and_10_out, and_11_out, and_12_out, and_13_out, and_14_out, and_15_out, not_1_out, not_2_out,
       not_3_out, not_4_out, not_5_out, not_6_out;

  not not_1 (not_1_out, Reset);
  and and_1 (and_1_out, IO_Enable, not_2_out);
  not not_2 (not_2_out, IO_Enable);
  not not_3 (not_3_out, _1_bit);
  not not_4 (not_4_out, _2_bit);
  not not_5 (not_5_out, _4_bit);
  not not_6 (not_6_out, _8_bit);
  D_Flip_Flop d_ff_1 (.clk(and_2_out), .D(not_1_out), .Q(A_C));  // open: Qn, preset, en, reset
  and and_2 (and_2_out, and_1_out, and_3_out);
  and and_3 (and_3_out, not_3_out, not_4_out, not_5_out, not_6_out);
  D_Flip_Flop d_ff_2 (.clk(and_4_out), .D(not_1_out), .Q(D0));  // open: Qn, preset, en, reset
  and and_4 (and_4_out, and_1_out, and_5_out);
  and and_5 (and_5_out, _1_bit, not_4_out, not_5_out, not_6_out);
  D_Flip_Flop d_ff_3 (.clk(and_6_out), .D(not_1_out), .Q(D1));  // open: Qn, preset, en, reset
  and and_6 (and_6_out, and_1_out, and_7_out);
  and and_7 (and_7_out, not_3_out, _2_bit, not_5_out, not_6_out);
  D_Flip_Flop d_ff_4 (.clk(and_8_out), .D(not_1_out), .Q(D2));  // open: Qn, preset, en, reset
  and and_8 (and_8_out, and_1_out, and_9_out);
  and and_9 (and_9_out, _1_bit, _2_bit, not_5_out, not_6_out);
  D_Flip_Flop d_ff_5 (.clk(and_10_out), .D(not_1_out), .Q(D3));  // open: Qn, preset, en, reset
  and and_10 (and_10_out, and_1_out, and_11_out);
  and and_11 (and_11_out, not_3_out, not_4_out, _4_bit, not_6_out);
  D_Flip_Flop d_ff_6 (.clk(and_12_out), .D(not_1_out), .Q(Engine_Starter));  // open: Qn, preset, en, reset
  and and_12 (and_12_out, and_1_out, and_13_out);
  and and_13 (and_13_out, _1_bit, not_4_out, _4_bit, not_6_out);
  D_Flip_Flop d_ff_7 (.clk(and_14_out), .D(not_1_out), .Q(Wipers));  // open: Qn, preset, en, reset
  and and_14 (and_14_out, and_1_out, and_15_out);
  and and_15 (and_15_out, not_3_out, _2_bit, _4_bit, not_6_out);
endmodule

module _7402 (
  input  _2,
  input  _3,
  input  _5,
  input  _6,
  input  _8,
  input  _9,
  input  _11,
  input  _12,
  output _1,
  output _4,
  output _10,
  output _13
);

  nor nor_1 (_1, _2, _3);
  nor nor_2 (_4, _5, _6);
  nor nor_3 (_10, _8, _9);
  nor nor_4 (_13, _11, _12);
endmodule

module _7408 (
  input  _1,
  input  _2,
  input  _4,
  input  _5,
  input  _9,
  input  _10,
  input  _12,
  input  _13,
  output _3,
  output _6,
  output _8,
  output _11
);

  and and_1 (_3, _1, _2);
  and and_2 (_6, _4, _5);
  and and_3 (_8, _9, _10);
  and and_4 (_11, _12, _13);
endmodule
