// Logisim project lab4.circ as structural Verilog: 1 circuit, main circuit main
module main (
  input  A0,
  input  A1,
  input  A2,
  input  A3,
  input  A4,
  input  A5,
  input  A6,
  input  A7,
  input  C0,
  input  C1,
  input  C2,
  input  D0,
  input  D1,
  input  D2,
  input  D3,
  input  D4,
  input  D5,
  input  D6,
  input  D7,
  output D0O,
  output D1O,
  output D2O,
  output D3O,
  output D4O,
  output D5O,
  output D6O,
  output D7O
);

  wire or_1_out, RAM_W_out, ROM_R_out;

  and and_1 (D0O, ROM_R_out, D7);
  and and_2 (D1O, ROM_R_out, D6);
  and and_3 (D2O, ROM_R_out, D5);
  and and_4 (D3O, ROM_R_out, D4);
  and and_5 (D4O, ROM_R_out, D3);
  and and_6 (D5O, ROM_R_out, D2);
  and and_7 (D6O, ROM_R_out, D1);
  and and_8 (D7O, ROM_R_out, D0);
  and ROM_R (ROM_R_out, C0, ~C1, ~C2);  // AND_Gate
  ROM rom_1 (.addr({A7, A6, A5, A4, A3, A2, A1, A0}), .data({D7, D6, D5, D4, D3, D2, D1, D0}), .sel(ROM_R_out));
  and RAM_R (ROM_R_out, ~C0, C1, ~C2);  // AND_Gate
  or or_1 (or_1_out, ROM_R_out, RAM_W_out);
  and RAM_W (RAM_W_out, C0, C1, ~C2);  // AND_Gate
  RAM #(.bus("asynch")) ram_1 (
    .addr({A7, A6, A5, A4, A3, A2, A1, A0}), .data({D7, D6, D5, D4, D3, D2, D1, D0}), .sel(or_1_out),
    .ld(RAM_W_out));  // open: clr

  // Notes on the sheet:
  //   contents of rom_1 (hex, n*v repeats v):
  //   11
endmodule
