// Logisim project cpu.circ as structural Verilog: 4 circuits, main circuit CPU
// Mem
module Memory (
  input  [7:0] Address,
  input  [7:0] Data_In,
  input  [1:0] Operation,
  output [7:0] Data_Out
);

  wire not_1_out, or_1_out, RAM_R_out, RAM_W_out, ROM_R_out;

  assign Data_Out = RAM_W_out ? Data_In : 8'bz;  // Controlled_Buffer controlled_buffer_1
  and ROM_R (ROM_R_out, Operation[0], ~Operation[1]);  // AND_Gate
  ROM rom_1 (.addr(Address), .data(Data_Out), .sel(ROM_R_out));
  and RAM_R (RAM_R_out, ~Operation[0], Operation[1]);  // AND_Gate
  or or_1 (or_1_out, RAM_R_out, RAM_W_out);
  not not_1 (not_1_out, RAM_W_out);
  and RAM_W (RAM_W_out, Operation[0], Operation[1]);
  RAM #(.bus("asynch")) ram_1 (.addr(Address), .data(Data_Out), .sel(or_1_out), .ld(not_1_out));  // open: clr

  // Notes on the sheet:
  //   contents of rom_1 (hex, n*v repeats v):
  //   4 0 1 4 4 2 4 1 3 2 31 0 4 2 3 2 31 1 4 3 3 2 31 2 4 4 3 2 31 3 4 4 3 2 32 0 4 3 3 2 32 1 4 2 3 2 32
  //   2 4 1 3 2 32 3 3 31 0 3 42 0 5 34 2 42 0 3 31 1 3 42 1 5 34 2 42 1 3 31 2 3 42 2 5 34 2 42 2 3 31 3
  //   3 42 3 5 34 2 42 3
endmodule

module CPU (
);

  wire ADD, and_1_out, and_2_out, and_3_out, and_4_out, Clear, clock_1_byte1, clock_1_byte2, clock_1_byte3,
       clock_1_fetch_reg_1, clock_1_fetch_reg_2, clock_1_instruction, Decode, Execute, MEMLD, MEMSET,
       PC_Update, R_dR, R_dW, REGSET, Write;
  wire [1:0] controlled_buffer_1_out, controlled_buffer_2_out, M_Select;
  wire [3:0] clock_1_clock_state, R_Addr, rA_R, rA_W, rB_R, rB_W;
  wire [7:0] adder_1_out, adder_2_out, adder_3_out, adder_4_out, adder_5_out, adder_6_out, adder_7_out,
       controlled_buffer_3_out, controlled_buffer_4_out, controlled_buffer_8_out, controlled_buffer_9_out,
       DataByte1, DataByte2, DataByte3, ExecResult_R, ExecResult_W, InstrByte, M_Addr, M_In, M_Out,
       MemLd_addr, MemSet_addr, nPC_In, nPC_Out, PC_In, PC_Out, pci_R, pci_W, pci_W_t, R_In, R_Out, rA_val,
       rB_val, val_R, val_W;
  wire [7:4] controlled_buffer_18_out;

  assign controlled_buffer_1_out = MEMSET ? 2'b11 : 2'bz;  // Controlled_Buffer controlled_buffer_1
  assign controlled_buffer_2_out = MEMLD ? 2'b10 : 2'bz;  // Controlled_Buffer controlled_buffer_2
  Adder adder_1 (.a(PC_Out), .b(8'h1), .out(adder_1_out));  // open: cin, cout
  Adder adder_2 (.a(PC_Out), .b(8'h2), .out(adder_2_out));  // open: cin, cout
  Adder adder_3 (.a(PC_Out), .b(8'h3), .out(adder_3_out));  // open: cin, cout
  assign controlled_buffer_3_out = MEMSET ? MemSet_addr : 8'bz;  // Controlled_Buffer controlled_buffer_3
  assign controlled_buffer_4_out = MEMLD ? MemLd_addr : 8'bz;  // Controlled_Buffer controlled_buffer_4
  Register #(.trigger("high")) register_1 (.D(ExecResult_W), .Q(ExecResult_R), .clk(Execute), .clr(Clear));  // open: en
  Register #(.width(4)) register_2 (.D(rA_W), .Q(rA_R), .clk(Decode), .clr(Clear));  // open: en
  Register #(.width(4)) register_3 (.D(rB_W), .Q(rB_R), .clk(Decode), .clr(Clear));  // open: en
  Register register_4 (.D(val_W), .Q(val_R), .clk(Decode), .clr(Clear));  // open: en
  Register register_5 (.D(pci_W_t), .Q(pci_R), .clk(Decode), .clr(Clear));  // open: en
  Multiplexer #(.select(4), .width(2)) multiplexer_1 (
    .in0(2'b00), .in1(2'b01), .in2(2'b01), .in3(2'b01), .in4(2'b01), .in8(controlled_buffer_2_out),
    .in9(controlled_buffer_1_out), .out(M_Select), .sel(clock_1_clock_state));  // open: in5, in6, in7, in10, in11, in12, in13, in14, in15, en
  Multiplexer #(.select(4), .width(8)) multiplexer_2 (
    .in1(PC_Out), .in2(adder_1_out), .in3(adder_2_out), .in4(adder_3_out), .in8(controlled_buffer_4_out),
    .in9(controlled_buffer_3_out), .out(M_Addr), .sel(clock_1_clock_state));  // open: in0, in5, in6, in7, in10, in11, in12, in13, in14, in15, en
  Clock clock_1 (
    .Clear(Clear), .Instruction(clock_1_instruction), .Byte1(clock_1_byte1), .Byte2(clock_1_byte2),
    .Byte3(clock_1_byte3), .Decode(Decode), .Fetch_Reg_1(clock_1_fetch_reg_1),
    .Fetch_Reg_2(clock_1_fetch_reg_2), .Execute(Execute), .Write(Write), .Clock_State(clock_1_clock_state),
    .Update_PC(PC_Update));
  Register #(.trigger("high")) register_6 (.D(PC_In), .Q(PC_Out), .clk(PC_Update));  // open: en, clr
  Register #(.trigger("high")) register_7 (.D(nPC_In), .Q(nPC_Out), .clk(Execute), .clr(Clear));  // open: en
  Memory memory_1 (.Address(M_Addr), .Data_Out(M_Out), .Data_In(M_In), .Operation(M_Select));
  Register #(.trigger("high")) register_8 (
    .D(M_Out), .Q(InstrByte), .clk(clock_1_instruction), .clr(Clear));  // open: en
  Register #(.trigger("high")) register_9 (.D(M_Out), .Q(DataByte1), .clk(clock_1_byte1), .clr(Clear));  // open: en
  Register #(.trigger("high")) register_10 (.D(M_Out), .Q(DataByte2), .clk(clock_1_byte2), .clr(Clear));  // open: en
  Register #(.trigger("high")) register_11 (.D(M_Out), .Q(DataByte3), .clk(clock_1_byte3), .clr(Clear));  // open: en
  assign PC_In = PC_Update ? nPC_Out : 8'bz;  // Controlled_Buffer controlled_buffer_5
  assign R_Addr = clock_1_fetch_reg_1 ? rA_R : 4'bz;  // Controlled_Buffer controlled_buffer_6
  or or_1 (R_dR, clock_1_fetch_reg_1, clock_1_fetch_reg_2);
  assign R_Addr = clock_1_fetch_reg_2 ? rB_R : 4'bz;  // Controlled_Buffer controlled_buffer_7
  and u_MEMSET (MEMSET, ~InstrByte[0], InstrByte[1], ~InstrByte[2], ~InstrByte[3], ~InstrByte[4], ~InstrByte[5], ~InstrByte[6], ~InstrByte[7]);  // AND_Gate
  and u_MEMLD (MEMLD, InstrByte[0], InstrByte[1], ~InstrByte[2], ~InstrByte[3], ~InstrByte[4], ~InstrByte[5], ~InstrByte[6], ~InstrByte[7]);  // AND_Gate
  Register_File register_file_1 (.Write_Data(R_In), .Addr(R_Addr), .Write(R_dW), .Read(R_dR), .Read_Data(R_Out));
  assign controlled_buffer_8_out = clock_1_fetch_reg_1 ? R_Out : 8'bz;  // Controlled_Buffer controlled_buffer_8
  assign controlled_buffer_9_out = clock_1_fetch_reg_2 ? R_Out : 8'bz;  // Controlled_Buffer controlled_buffer_9
  and u_REGSET (REGSET, ~InstrByte[0], ~InstrByte[1], InstrByte[2], ~InstrByte[3], ~InstrByte[4], ~InstrByte[5], ~InstrByte[6], ~InstrByte[7]);  // AND_Gate
  Adder adder_4 (.a(pci_R), .b(PC_Out), .out(adder_4_out));  // open: cin, cout
  Register #(.trigger("high")) register_12 (
    .D(controlled_buffer_8_out), .Q(rA_val), .clk(clock_1_fetch_reg_1), .clr(Clear));  // open: en
  Register #(.trigger("high")) register_13 (
    .D(controlled_buffer_9_out), .Q(rB_val), .clk(clock_1_fetch_reg_2), .clr(Clear));  // open: en
  and u_ADD (ADD, InstrByte[0], ~InstrByte[1], InstrByte[2], ~InstrByte[3], ~InstrByte[4], ~InstrByte[5], ~InstrByte[6], ~InstrByte[7]);  // AND_Gate
  assign nPC_In = Execute ? adder_4_out : 8'bz;  // Controlled_Buffer controlled_buffer_10
  assign {rB_W, rA_W} = MEMSET ? DataByte1 : 8'bz;  // Controlled_Buffer controlled_buffer_11
  assign val_W = MEMSET ? DataByte2 : 8'bz;  // Controlled_Buffer controlled_buffer_12
  assign pci_W = MEMSET ? 8'h3 : 8'bz;  // Controlled_Buffer controlled_buffer_13
  assign {rB_W, rA_W} = MEMLD ? DataByte1 : 8'bz;  // Controlled_Buffer controlled_buffer_14
  assign val_W = MEMLD ? DataByte2 : 8'bz;  // Controlled_Buffer controlled_buffer_15
  assign pci_W = MEMLD ? 8'h3 : 8'bz;  // Controlled_Buffer controlled_buffer_16
  assign val_W = REGSET ? DataByte1 : 8'bz;  // Controlled_Buffer controlled_buffer_17
  assign {controlled_buffer_18_out, rA_W} = REGSET ? DataByte2 : 8'bz;  // Controlled_Buffer controlled_buffer_18
  assign pci_W = REGSET ? 8'h3 : 8'bz;  // Controlled_Buffer controlled_buffer_19
  assign {rB_W, rA_W} = ADD ? DataByte1 : 8'bz;  // Controlled_Buffer controlled_buffer_20
  assign pci_W = ADD ? 8'h2 : 8'bz;  // Controlled_Buffer controlled_buffer_21
  assign ExecResult_W = MEMSET ? adder_5_out : 8'bz;  // Controlled_Buffer controlled_buffer_22
  Adder adder_5 (.a(rA_val), .b(val_R), .out(adder_5_out));  // open: cin, cout
  assign MemLd_addr = MEMLD ? adder_6_out : 8'bz;  // Controlled_Buffer controlled_buffer_23
  Adder adder_6 (.a(rA_val), .b(val_R), .out(adder_6_out));  // open: cin, cout
  assign ExecResult_W = MEMLD ? M_Out : 8'bz;  // Controlled_Buffer controlled_buffer_24
  assign ExecResult_W = REGSET ? val_R : 8'bz;  // Controlled_Buffer controlled_buffer_25
  assign ExecResult_W = ADD ? adder_7_out : 8'bz;  // Controlled_Buffer controlled_buffer_26
  Adder adder_7 (.a(rA_val), .b(rB_val), .out(adder_7_out));  // open: cin, cout
  and and_1 (and_1_out, MEMSET, Write);
  and and_2 (and_2_out, MEMLD, Write);
  assign R_In = and_2_out ? ExecResult_R : 8'bz;  // Controlled_Buffer controlled_buffer_27
  assign R_Addr = and_2_out ? rB_R : 4'bz;  // Controlled_Buffer controlled_buffer_28
  and and_3 (and_3_out, REGSET, Write);
  and and_4 (and_4_out, ADD, Write);
  assign MemSet_addr = and_1_out ? ExecResult_R : 8'bz;  // Controlled_Buffer controlled_buffer_29
  assign M_In = and_1_out ? rB_val : 8'bz;  // Controlled_Buffer controlled_buffer_30
  assign R_In = and_3_out ? ExecResult_R : 8'bz;  // Controlled_Buffer controlled_buffer_31
  assign R_Addr = and_3_out ? rA_R : 4'bz;  // Controlled_Buffer controlled_buffer_32
  assign R_In = and_4_out ? ExecResult_R : 8'bz;  // Controlled_Buffer controlled_buffer_33
  assign R_Addr = and_4_out ? rA_R : 4'bz;  // Controlled_Buffer controlled_buffer_34
  ExactlyOne xor_1 (.out(R_dW), .in0(and_2_out), .in1(and_3_out), .in2(and_4_out));
endmodule

// Reg
module Register_File (
  input  [7:0] Write_Data,
  input  [3:0] Addr,
  input  Write,
  input  Read,
  output [7:0] Read_Data
);

  wire decoder_1_out1, decoder_1_out2, decoder_1_out3, decoder_1_out4, decoder_1_out6, decoder_1_out7,
       decoder_1_out8, decoder_1_out9, xor_1_out;
  wire [3:0] adder_1_out, controlled_buffer_1_out, controlled_buffer_3_out;
  wire [7:0] register_1_q, register_2_q, register_3_q, register_4_q;

  xor xor_1 (xor_1_out, Write, Read);
  assign controlled_buffer_1_out = Write ? 4'b0101 : 4'bz;  // Controlled_Buffer controlled_buffer_1
  assign controlled_buffer_1_out = Read ? 4'b0000 : 4'bz;  // Controlled_Buffer controlled_buffer_2
  assign controlled_buffer_3_out = xor_1_out ? adder_1_out : 4'bz;  // Controlled_Buffer controlled_buffer_3
  Adder #(.width(4)) adder_1 (.a(Addr), .b(controlled_buffer_1_out), .out(adder_1_out));  // open: cin, cout
  Decoder #(.select(4)) decoder_1 (
    .out1(decoder_1_out1), .out2(decoder_1_out2), .out3(decoder_1_out3), .out4(decoder_1_out4),
    .out6(decoder_1_out6), .out7(decoder_1_out7), .out8(decoder_1_out8), .out9(decoder_1_out9),
    .sel(controlled_buffer_3_out));  // open: out0, out5, out10, out11, out12, out13, out14, out15, en
  Register #(.trigger("high")) register_1 (.D(Write_Data), .Q(register_1_q), .clk(decoder_1_out6));  // open: en, clr
  assign Read_Data = decoder_1_out1 ? register_1_q : 8'bz;  // Controlled_Buffer controlled_buffer_4
  assign Read_Data = decoder_1_out2 ? register_2_q : 8'bz;  // Controlled_Buffer controlled_buffer_5
  Register #(.trigger("high")) register_2 (.D(Write_Data), .Q(register_2_q), .clk(decoder_1_out7));  // open: en, clr
  Register #(.trigger("high")) register_3 (.D(Write_Data), .Q(register_3_q), .clk(decoder_1_out8));  // open: en, clr
  assign Read_Data = decoder_1_out3 ? register_3_q : 8'bz;  // Controlled_Buffer controlled_buffer_6
  Register #(.trigger("high")) register_4 (.D(Write_Data), .Q(register_4_q), .clk(decoder_1_out9));  // open: en, clr
  assign Read_Data = decoder_1_out4 ? register_4_q : 8'bz;  // Controlled_Buffer controlled_buffer_7
endmodule

module Clock (
  output Clear,
  output Instruction,
  output Byte1,
  output Byte2,
  output Byte3,
  output Decode,
  output Fetch_Reg_1,
  output Fetch_Reg_2,
  output Execute,
  output Write,
  output Update_PC,
  output [3:0] Clock_State
);

  wire clock_1_out, clock_2_out, decoder_1_out0, decoder_1_out1, decoder_1_out2, decoder_1_out3,
       decoder_1_out4, decoder_1_out5, decoder_1_out6, decoder_1_out7, decoder_1_out8, decoder_1_out9,
       decoder_1_out10, not_1_out;
  wire [3:0] adder_1_out, controlled_buffer_1_out;

  Register #(.width(4)) register_1 (.D(controlled_buffer_1_out), .Q(Clock_State), .clk(clock_1_out));  // open: en, clr
  Clock_part clock_1 (.out(clock_1_out));
  Decoder #(.select(4)) decoder_1 (
    .out0(decoder_1_out0), .out1(decoder_1_out1), .out2(decoder_1_out2), .out3(decoder_1_out3),
    .out4(decoder_1_out4), .out5(decoder_1_out5), .out6(decoder_1_out6), .out7(decoder_1_out7),
    .out8(decoder_1_out8), .out9(decoder_1_out9), .out10(decoder_1_out10), .sel(Clock_State));  // open: out11, out12, out13, out14, out15, en
  Clock_part clock_2 (.out(clock_2_out));
  Adder #(.width(4)) adder_1 (.a(Clock_State), .b(4'b0001), .out(adder_1_out));  // open: cin, cout
  assign controlled_buffer_1_out = not_1_out ? adder_1_out : 4'bz;  // Controlled_Buffer controlled_buffer_1
  not not_1 (not_1_out, decoder_1_out10);
  assign controlled_buffer_1_out = decoder_1_out10 ? 4'b0000 : 4'bz;  // Controlled_Buffer controlled_buffer_2
  and and_1 (Clear, decoder_1_out0, clock_2_out);
  and and_2 (Instruction, decoder_1_out1, clock_2_out);
  and and_3 (Byte1, decoder_1_out2, clock_2_out);
  and and_4 (Byte2, decoder_1_out3, clock_2_out);
  and and_5 (Byte3, decoder_1_out4, clock_2_out);
  and and_6 (Decode, decoder_1_out5, clock_2_out);
  and and_7 (Fetch_Reg_1, decoder_1_out6, clock_2_out);
  and and_8 (Fetch_Reg_2, decoder_1_out7, clock_2_out);
  and and_9 (Execute, decoder_1_out8, clock_2_out);
  and and_10 (Write, decoder_1_out9, clock_2_out);
  and and_11 (Update_PC, decoder_1_out10, clock_2_out);
endmodule
